// Logisim project alu.circ as structural Verilog: 2 circuits, main circuit alu
module alu (
  input  [31:0] A,
  input  [31:0] B,
  input  [3:0] ALUSel,
  output [31:0] Result
);

  wire comparator_1_lt, xor_2_out;
  wire [4:0] bit_extender_1_out, bit_extender_2_out, bit_extender_3_out;
  wire [31:0] absolute_1_out_2, absolute_2_out_2, add0, and0, divu0, mul0, mulh0, mulhu0, multiplier_2_cout,
       not_1_out, or0, remu0, sll0, slt0, sra0, srl0, sub0, xor0;

  Bit_Extender #(.in_width(32), .out_width(5)) bit_extender_1 (.in(B), .out(bit_extender_1_out));
  Bit_Extender #(.in_width(32), .out_width(5)) bit_extender_2 (.in(B), .out(bit_extender_2_out));
  Bit_Extender #(.in_width(32), .out_width(5)) bit_extender_3 (.in(B), .out(bit_extender_3_out));
  Comparator #(.width(32)) comparator_1 (.a(A), .b(B), .lt(comparator_1_lt));  // open: gt, eq
  Adder #(.width(32)) adder_1 (.a(A), .b(B), .out(add0));  // open: cin, cout
  assign and0 = A & B;  // AND_Gate and_1, 32 bits wide
  assign or0 = A | B;  // OR_Gate or_1, 32 bits wide
  assign xor0 = A ^ B;  // XOR_Gate xor_1, 32 bits wide
  Shifter #(.width(32), .shift("lr")) shifter_1 (.in(A), .\dist (bit_extender_1_out), .out(srl0));
  Shifter #(.width(32), .shift("ar")) shifter_2 (.in(A), .\dist (bit_extender_2_out), .out(sra0));
  Shifter #(.width(32)) shifter_3 (.in(A), .\dist (bit_extender_3_out), .out(sll0));
  assign slt0 = {{31{1'b0}}, comparator_1_lt};  // Bit_Extender bit_extender_4
  Divider #(.width(32)) divider_1 (.a(A), .b(B), .out(divu0), .rem(remu0));  // open: upper
  Multiplier #(.width(32)) multiplier_1 (.a(A), .b(B), .out(mul0), .cout(mulhu0));  // open: cin
  Subtractor #(.width(32)) subtractor_1 (.a(A), .b(B), .out(sub0));  // open: bin, bout
  absolute absolute_1 (.in_1(A), .out_2(absolute_1_out_2));
  absolute absolute_2 (.in_1(B), .out_2(absolute_2_out_2));
  xor xor_2 (xor_2_out, A[31], B[31]);
  Multiplier #(.width(32)) multiplier_2 (
    .a(absolute_1_out_2), .b(absolute_2_out_2), .cout(multiplier_2_cout));  // open: out, cin
  assign not_1_out = ~multiplier_2_cout;  // NOT_Gate not_1, 32 bits wide
  Multiplexer #(.width(32), .enable("false")) multiplexer_1 (
    .in0(multiplier_2_cout), .in1(not_1_out), .out(mulh0), .sel(xor_2_out));
  Multiplexer #(.select(4), .width(32), .enable("false")) multiplexer_2 (
    .in0(add0), .in1(and0), .in2(or0), .in3(xor0), .in4(srl0), .in5(sra0), .in6(sll0), .in7(slt0),
    .in8(divu0), .in9(remu0), .in10(mul0), .in11(mulhu0), .in12(sub0), .in13(B), .in14(mulh0), .out(Result),
    .sel(ALUSel));  // open: in15

  // Other names for the same wires on the sheet: bsel0[31:0] = B

  // Notes on the sheet:
  //   INPUTS to your circuit
  //   DON'T CHANGE THE LOCATIONS OF THE INPUTS AND OUTPUTS!
  //   OUTPUT from your circuit
endmodule

module absolute (
  input  [31:0] in_1,
  output [31:0] out_2
);

  wire [31:0] negator_1_out;

  Negator #(.width(32)) negator_1 (.in(in_1), .out(negator_1_out));
  Multiplexer #(.width(32), .enable("false")) multiplexer_1 (
    .in0(in_1), .in1(negator_1_out), .out(out_2), .sel(in_1[31]));
endmodule
