// Logisim project branch_comp.circ as structural Verilog: 1 circuit, main circuit branch_comp
module branch_comp (
  input  [31:0] rs1,
  input  [31:0] rs2,
  input  BrUn,
  output BrEq,
  output BrLt
);

  wire [1:0] comparator_1_eq, comparator_2_eq;

  Comparator #(.width(32)) comparator_1 (
    .a(rs1), .b(rs2), .eq(comparator_1_eq[0]), .lt(comparator_1_eq[1]));  // open: gt
  Comparator #(.width(32), .mode("unsigned")) comparator_2 (
    .a(rs1), .b(rs2), .eq(comparator_2_eq[0]), .lt(comparator_2_eq[1]));  // open: gt
  Multiplexer #(.width(2), .enable("false")) multiplexer_1 (
    .in0(comparator_1_eq), .in1(comparator_2_eq), .out({BrLt, BrEq}), .sel(BrUn));

  // Notes on the sheet:
  //   INPUTS to your circuit
  //   DON'T CHANGE THE LOCATIONS OF THE INPUTS AND OUTPUTS!
  //   OUTPUT from your circuit
endmodule
