// Logisim project control_logic.circ as structural Verilog: 1 circuit, main circuit control_logic
module control_logic (
  input  [31:0] inst,
  input  BrEq,
  input  BrLt,
  output PCSel,
  output RegWEn,
  output [2:0] ImmSel,
  output BrUn,
  output ASel,
  output BSel,
  output [3:0] ALUSel,
  output MemRW,
  output [1:0] WBSel
);

  wire and_3_out, and_4_out, and_5_out, and_6_out, and_7_out, and_8_out, comparator_1_eq, comparator_2_eq,
       comparator_3_eq, comparator_4_eq, comparator_5_eq, comparator_6_eq, comparator_7_eq, comparator_8_eq,
       comparator_9_eq, comparator_10_eq, comparator_11_eq, comparator_12_eq, comparator_14_eq,
       comparator_15_eq, comparator_16_eq, comparator_17_eq, comparator_18_eq, comparator_19_eq,
       comparator_20_eq, comparator_21_eq, comparator_22_eq, comparator_23_eq, comparator_24_eq,
       comparator_25_eq, comparator_26_eq, comparator_27_eq, comparator_28_eq, comparator_30_eq,
       comparator_32_eq, comparator_33_eq, comparator_34_eq, comparator_35_eq, comparator_36_eq,
       comparator_38_eq, comparator_39_eq, comparator_40_eq, comparator_41_eq, comparator_42_eq,
       comparator_43_eq, comparator_44_eq, comparator_45_eq, comparator_46_eq, comparator_47_eq,
       comparator_48_eq, comparator_49_eq, comparator_50_eq, comparator_51_eq, comparator_52_eq,
       comparator_53_eq, comparator_54_eq, comparator_56_eq, comparator_57_eq, comparator_58_eq,
       comparator_59_eq, comparator_60_eq, comparator_61_eq, comparator_62_eq, comparator_63_eq, is_divu,
       is_mul, is_mulh, is_mulhu, is_remu, is_sub, not_1_out, not_2_out, not_3_out, or_2_out, or_3_out,
       or_4_out, or_10_out, or_12_out, PCSel_SB;
  wire [2:0] or_11_out;
  wire [3:0] ALUSel_RI, multiplexer_3_out, multiplexer_4_out, multiplexer_5_out, multiplexer_6_out,
       multiplexer_8_out, multiplexer_9_out, multiplexer_10_out;
  wire [4:0] or_8_out;

  Comparator #(.width(7)) comparator_1 (.a(7'b1100011), .b(inst[6:0]), .eq(comparator_1_eq));  // open: gt, lt
  Comparator #(.width(3)) comparator_2 (.a(3'b110), .b(inst[14:12]), .eq(comparator_2_eq));  // open: gt, lt
  Comparator #(.width(3)) comparator_3 (.a(3'b111), .b(inst[14:12]), .eq(comparator_3_eq));  // open: gt, lt
  Comparator #(.width(7)) comparator_4 (.a(7'b1100011), .b(inst[6:0]), .eq(comparator_4_eq));  // open: gt, lt
  or or_1 (PCSel, PCSel_SB, comparator_5_eq, comparator_6_eq);
  Comparator #(.width(7)) comparator_5 (.a(7'b1101111), .b(inst[6:0]), .eq(comparator_5_eq));  // open: gt, lt
  Comparator #(.width(7)) comparator_6 (.a(7'b1100111), .b(inst[6:0]), .eq(comparator_6_eq));  // open: gt, lt
  and and_1 (BrUn, comparator_1_eq, or_2_out);
  or or_2 (or_2_out, comparator_2_eq, comparator_3_eq);
  and and_2 (PCSel_SB, comparator_4_eq, or_3_out);
  Comparator #(.width(3)) comparator_7 (.a(3'b000), .b(inst[14:12]), .eq(comparator_7_eq));  // open: gt, lt
  Comparator #(.width(3)) comparator_8 (.a(3'b001), .b(inst[14:12]), .eq(comparator_8_eq));  // open: gt, lt
  not not_1 (not_1_out, BrEq);
  Comparator #(.width(3)) comparator_9 (.a(3'b100), .b(inst[14:12]), .eq(comparator_9_eq));  // open: gt, lt
  Comparator #(.width(3)) comparator_10 (.a(3'b101), .b(inst[14:12]), .eq(comparator_10_eq));  // open: gt, lt
  not not_2 (not_2_out, BrLt);
  Comparator #(.width(3)) comparator_11 (.a(3'b110), .b(inst[14:12]), .eq(comparator_11_eq));  // open: gt, lt
  Comparator #(.width(3)) comparator_12 (.a(3'b111), .b(inst[14:12]), .eq(comparator_12_eq));  // open: gt, lt
  not not_3 (not_3_out, BrLt);
  or or_3 (or_3_out, and_3_out, and_4_out, and_5_out, and_6_out, and_7_out, and_8_out);
  and and_3 (and_3_out, comparator_7_eq, BrEq);
  and and_4 (and_4_out, comparator_8_eq, not_1_out);
  and and_5 (and_5_out, comparator_9_eq, BrLt);
  and and_6 (and_6_out, comparator_10_eq, not_2_out);
  and and_7 (and_7_out, comparator_11_eq, BrLt);
  and and_8 (and_8_out, comparator_12_eq, not_3_out);
  Comparator #(.width(7)) comparator_13 (.a(7'b1101111), .b(inst[6:0]), .eq(or_8_out[4]));  // open: gt, lt
  not not_4 (RegWEn, or_4_out);
  or or_4 (or_4_out, comparator_14_eq, comparator_15_eq);
  Comparator #(.width(7)) comparator_14 (.a(7'b0100011), .b(inst[6:0]), .eq(comparator_14_eq));  // open: gt, lt
  Comparator #(.width(7)) comparator_15 (.a(7'b1100011), .b(inst[6:0]), .eq(comparator_15_eq));  // open: gt, lt
  or or_5 (ASel, PCSel_SB, comparator_16_eq, comparator_17_eq, comparator_18_eq);
  Comparator #(.width(7)) comparator_16 (.a(7'b0010111), .b(inst[6:0]), .eq(comparator_16_eq));  // open: gt, lt
  Comparator #(.width(7)) comparator_17 (.a(7'b0110111), .b(inst[6:0]), .eq(comparator_17_eq));  // open: gt, lt
  Comparator #(.width(7)) comparator_18 (.a(7'b1101111), .b(inst[6:0]), .eq(comparator_18_eq));  // open: gt, lt
  or or_6 (or_8_out[3], comparator_19_eq, comparator_20_eq);
  Comparator #(.width(7)) comparator_19 (.a(7'b0010111), .b(inst[6:0]), .eq(comparator_19_eq));  // open: gt, lt
  Comparator #(.width(7)) comparator_20 (.a(7'b0110111), .b(inst[6:0]), .eq(comparator_20_eq));  // open: gt, lt
  Comparator #(.width(7)) comparator_21 (.a(7'b0000011), .b(inst[6:0]), .eq(comparator_21_eq));  // open: gt, lt
  Comparator #(.width(7)) comparator_22 (.a(7'b0010011), .b(inst[6:0]), .eq(comparator_22_eq));  // open: gt, lt
  Comparator #(.width(7)) comparator_23 (.a(7'b0100011), .b(inst[6:0]), .eq(comparator_23_eq));  // open: gt, lt
  Comparator #(.width(7)) comparator_24 (.a(7'b1100011), .b(inst[6:0]), .eq(comparator_24_eq));  // open: gt, lt
  Comparator #(.width(7)) comparator_25 (.a(7'b0010111), .b(inst[6:0]), .eq(comparator_25_eq));  // open: gt, lt
  Comparator #(.width(7)) comparator_26 (.a(7'b0110111), .b(inst[6:0]), .eq(comparator_26_eq));  // open: gt, lt
  Comparator #(.width(7)) comparator_27 (.a(7'b1101111), .b(inst[6:0]), .eq(comparator_27_eq));  // open: gt, lt
  Comparator #(.width(7)) comparator_28 (.a(7'b1100111), .b(inst[6:0]), .eq(comparator_28_eq));  // open: gt, lt
  Multiplexer #(.select(5), .width(3), .enable("false")) multiplexer_1 (
    .in1(3'b000), .in2(3'b001), .in4(3'b010), .in8(3'b011), .in16(3'b100), .out(ImmSel), .sel(or_8_out));  // open: in0, in3, in5, in6, in7, in9, in10, in11, in12, in13, in14, in15, in17, in18, in19, in20, in21, in22, in23, in24, in25, in26, in27, in28, in29, in30, in31
  or or_7 (BSel, comparator_21_eq, comparator_22_eq, comparator_23_eq, comparator_24_eq, comparator_25_eq, comparator_26_eq, comparator_27_eq, comparator_28_eq);
  Comparator #(.width(7)) comparator_29 (.a(7'b1100011), .b(inst[6:0]), .eq(or_8_out[2]));  // open: gt, lt
  Comparator #(.width(7)) comparator_30 (.a(7'b0110011), .b(inst[6:0]), .eq(comparator_30_eq));  // open: gt, lt
  Comparator #(.width(7)) comparator_31 (.a(7'b0100011), .b(inst[6:0]), .eq(or_8_out[1]));  // open: gt, lt
  and and_9 (is_mul, comparator_30_eq, comparator_32_eq, comparator_33_eq);
  Comparator #(.width(3)) comparator_32 (.a(3'b000), .b(inst[14:12]), .eq(comparator_32_eq));  // open: gt, lt
  Comparator #(.width(7)) comparator_33 (.a(7'b0000001), .b(inst[31:25]), .eq(comparator_33_eq));  // open: gt, lt
  and and_10 (is_mulhu, comparator_34_eq, comparator_35_eq, comparator_36_eq);
  Comparator #(.width(7)) comparator_34 (.a(7'b0110011), .b(inst[6:0]), .eq(comparator_34_eq));  // open: gt, lt
  Comparator #(.width(3)) comparator_35 (.a(3'b011), .b(inst[14:12]), .eq(comparator_35_eq));  // open: gt, lt
  Comparator #(.width(7)) comparator_36 (.a(7'b0000001), .b(inst[31:25]), .eq(comparator_36_eq));  // open: gt, lt
  Comparator #(.width(7)) comparator_37 (.a(7'b0100011), .b(inst[6:0]), .eq(MemRW));  // open: gt, lt
  or or_8 (or_8_out[0], comparator_38_eq, comparator_40_eq, comparator_39_eq);
  Comparator #(.width(7)) comparator_38 (.a(7'b0000011), .b(inst[6:0]), .eq(comparator_38_eq));  // open: gt, lt
  Comparator #(.width(7)) comparator_39 (.a(7'b0010011), .b(inst[6:0]), .eq(comparator_39_eq));  // open: gt, lt
  Comparator #(.width(7)) comparator_40 (.a(7'b1100111), .b(inst[6:0]), .eq(comparator_40_eq));  // open: gt, lt
  Comparator #(.width(7)) comparator_41 (.a(7'b0110011), .b(inst[6:0]), .eq(comparator_41_eq));  // open: gt, lt
  Comparator #(.width(3)) comparator_42 (.a(3'b000), .b(inst[14:12]), .eq(comparator_42_eq));  // open: gt, lt
  Comparator #(.width(7)) comparator_43 (.a(7'b0100000), .b(inst[31:25]), .eq(comparator_43_eq));  // open: gt, lt
  Comparator #(.width(7)) comparator_44 (.a(7'b0110011), .b(inst[6:0]), .eq(comparator_44_eq));  // open: gt, lt
  and and_11 (is_sub, comparator_41_eq, comparator_42_eq, comparator_43_eq);
  and and_12 (is_divu, comparator_44_eq, comparator_45_eq, comparator_46_eq);
  Comparator #(.width(3)) comparator_45 (.a(3'b101), .b(inst[14:12]), .eq(comparator_45_eq));  // open: gt, lt
  Comparator #(.width(7)) comparator_46 (.a(7'b0000001), .b(inst[31:25]), .eq(comparator_46_eq));  // open: gt, lt
  Comparator #(.width(7)) comparator_47 (.a(7'b1101111), .b(inst[6:0]), .eq(comparator_47_eq));  // open: gt, lt
  Comparator #(.width(7)) comparator_48 (.a(7'b1100111), .b(inst[6:0]), .eq(comparator_48_eq));  // open: gt, lt
  Comparator #(.width(7)) comparator_49 (.a(7'b0110011), .b(inst[6:0]), .eq(comparator_49_eq));  // open: gt, lt
  Comparator #(.width(7)) comparator_50 (.a(7'b0110011), .b(inst[6:0]), .eq(comparator_50_eq));  // open: gt, lt
  or or_9 (or_11_out[2], comparator_47_eq, comparator_48_eq);
  and and_13 (is_mulh, comparator_49_eq, comparator_51_eq, comparator_52_eq);
  Comparator #(.width(3)) comparator_51 (.a(3'b001), .b(inst[14:12]), .eq(comparator_51_eq));  // open: gt, lt
  Comparator #(.width(7)) comparator_52 (.a(7'b0000001), .b(inst[31:25]), .eq(comparator_52_eq));  // open: gt, lt
  and and_14 (is_remu, comparator_50_eq, comparator_53_eq, comparator_54_eq);
  Comparator #(.width(3)) comparator_53 (.a(3'b111), .b(inst[14:12]), .eq(comparator_53_eq));  // open: gt, lt
  Comparator #(.width(7)) comparator_54 (.a(7'b0000001), .b(inst[31:25]), .eq(comparator_54_eq));  // open: gt, lt
  Comparator #(.width(7)) comparator_55 (.a(7'b0000011), .b(inst[6:0]), .eq(or_11_out[1]));  // open: gt, lt
  Multiplexer #(.select(3), .width(2), .enable("false")) multiplexer_2 (
    .in1(2'b00), .in2(2'b01), .in4(2'b10), .out(WBSel), .sel(or_11_out));  // open: in0, in3, in5, in6, in7
  Multiplexer #(.select(3), .width(4), .enable("false")) multiplexer_3 (
    .in0(4'b0000), .in1(4'b0110), .in2(4'b0111), .in3(4'b0011), .in4(4'b0100), .in5(4'b0101), .in6(4'b0010),
    .in7(4'b0001), .out(multiplexer_3_out), .sel(inst[14:12]));
  or or_10 (or_10_out, comparator_56_eq, comparator_57_eq);
  Comparator #(.width(7)) comparator_56 (.a(7'b0110011), .b(inst[6:0]), .eq(comparator_56_eq));  // open: gt, lt
  Comparator #(.width(7)) comparator_57 (.a(7'b0010011), .b(inst[6:0]), .eq(comparator_57_eq));  // open: gt, lt
  or or_11 (or_11_out[0], comparator_58_eq, comparator_59_eq, comparator_60_eq, comparator_61_eq);
  Comparator #(.width(7)) comparator_58 (.a(7'b0110011), .b(inst[6:0]), .eq(comparator_58_eq));  // open: gt, lt
  Comparator #(.width(7)) comparator_59 (.a(7'b0010011), .b(inst[6:0]), .eq(comparator_59_eq));  // open: gt, lt
  Comparator #(.width(7)) comparator_60 (.a(7'b0010111), .b(inst[6:0]), .eq(comparator_60_eq));  // open: gt, lt
  Comparator #(.width(7)) comparator_61 (.a(7'b0110111), .b(inst[6:0]), .eq(comparator_61_eq));  // open: gt, lt
  Multiplexer #(.width(4), .enable("false")) multiplexer_4 (
    .in0(multiplexer_3_out), .in1(4'b1010), .out(multiplexer_4_out), .sel(is_mul));
  Multiplexer #(.width(4), .enable("false")) multiplexer_5 (
    .in0(4'b0000), .in1(ALUSel_RI), .out(multiplexer_5_out), .sel(or_10_out));
  Multiplexer #(.width(4), .enable("false")) multiplexer_6 (
    .in0(multiplexer_4_out), .in1(4'b1100), .out(multiplexer_6_out), .sel(is_sub));
  Multiplexer #(.width(4), .enable("false")) multiplexer_7 (
    .in0(multiplexer_5_out), .in1(4'b1101), .out(ALUSel), .sel(or_12_out));
  Multiplexer #(.width(4), .enable("false")) multiplexer_8 (
    .in0(multiplexer_6_out), .in1(4'b1110), .out(multiplexer_8_out), .sel(is_mulh));
  or or_12 (or_12_out, comparator_62_eq, comparator_63_eq);
  Comparator #(.width(7)) comparator_62 (.a(7'b0010111), .b(inst[6:0]), .eq(comparator_62_eq));  // open: gt, lt
  Comparator #(.width(7)) comparator_63 (.a(7'b0110111), .b(inst[6:0]), .eq(comparator_63_eq));  // open: gt, lt
  Multiplexer #(.width(4), .enable("false")) multiplexer_9 (
    .in0(multiplexer_8_out), .in1(4'b1011), .out(multiplexer_9_out), .sel(is_mulhu));
  Multiplexer #(.width(4), .enable("false")) multiplexer_10 (
    .in0(multiplexer_9_out), .in1(4'b1000), .out(multiplexer_10_out), .sel(is_divu));
  Multiplexer #(.width(4), .enable("false")) multiplexer_11 (
    .in0(multiplexer_10_out), .in1(4'b1001), .out(ALUSel_RI), .sel(is_remu));

  // Other names for the same wires on the sheet: Opcode[6:0] = inst[6:0]; funct3[2:0] = inst[14:12];
  //   funct7[6:0] = inst[31:25]

  // Notes on the sheet:
  //   INPUTS to your circuit
  //   DON'T CHANGE THE LOCATIONS OF THE INPUTS AND OUTPUTS!
  //   OUTPUT from your circuit
endmodule
