// Logisim project cpu.circ as structural Verilog: 1 circuit, main circuit main
module main (
  input  [31:0] INSTRUCTION,
  input  CLOCK,
  output [31:0] PROGRAM_COUNTER,
  output [31:0] ra,
  output [31:0] sp,
  output [31:0] t0,
  output [31:0] t1,
  output [31:0] t2,
  output [31:0] s0,
  output [31:0] s1,
  output [31:0] a0
);

  wire branch_comp_1_breq, branch_comp_1_brlt, control_logic_1_asel, control_logic_1_brun,
       control_logic_1_bsel, control_logic_1_memrw, control_logic_1_pcsel, control_logic_1_regwen;
  wire [1:0] control_logic_1_wbsel;
  wire [2:0] control_logic_1_immsel;
  wire [3:0] control_logic_1_alusel;
  wire [31:0] ALU_RESULT, DMEM_READ_DATA, IMM, INST, multiplexer_1_out, multiplexer_2_out, multiplexer_3_out,
       multiplexer_4_out, PC_PLUS_4, RegFile_read_data_1, RegFile_read_data_2, register_2_q, register_3_q,
       WB_DATA;

  control_logic control_logic_1 (
    .BSel(control_logic_1_bsel), .BrUn(control_logic_1_brun), .RegWEn(control_logic_1_regwen),
    .ImmSel(control_logic_1_immsel), .ASel(control_logic_1_asel), .PCSel(control_logic_1_pcsel),
    .BrLt(branch_comp_1_brlt), .BrEq(branch_comp_1_breq), .inst(INST), .ALUSel(control_logic_1_alusel),
    .MemRW(control_logic_1_memrw), .WBSel(control_logic_1_wbsel));
  Adder #(.width(32)) adder_1 (.a(PROGRAM_COUNTER), .b(32'h4), .out(PC_PLUS_4));  // open: cin, cout
  Register #(.width(32)) PC (.D(multiplexer_1_out), .en(1'b1), .clk(CLOCK), .Q(PROGRAM_COUNTER));  // open: clr
  Multiplexer #(.width(32), .enable("false")) multiplexer_1 (
    .in0(PC_PLUS_4), .in1(ALU_RESULT), .out(multiplexer_1_out), .sel(control_logic_1_pcsel));
  Multiplexer #(.width(32), .enable("false")) multiplexer_2 (
    .in0(INSTRUCTION), .in1(32'h13), .out(multiplexer_2_out), .sel(control_logic_1_pcsel));
  Register #(.width(32)) register_1 (.D(multiplexer_2_out), .clk(CLOCK), .Q(INST));  // open: en, clr
  imm_gen imm_gen_1 (.ImmSel(control_logic_1_immsel), .inst(INST), .imm(IMM));
  regfile_main RegFile (
    .rs2(INST[24:20]), .rd(INST[11:7]), .Read_Data_1(RegFile_read_data_1), .Read_Data_2(RegFile_read_data_2),
    .ra(ra), .sp(sp), .t0(t0), .t1(t1), .t2(t2), .s0(s0), .s1(s1), .a0(a0), .rs1(INST[19:15]),
    .Write_Data(WB_DATA), .RegWEn(control_logic_1_regwen), .clk(CLOCK));
  Register #(.width(32)) register_2 (.D(PROGRAM_COUNTER), .clk(CLOCK), .Q(register_2_q));  // open: en, clr
  branch_comp branch_comp_1 (
    .BrEq(branch_comp_1_breq), .BrUn(control_logic_1_brun), .rs1(RegFile_read_data_1),
    .BrLt(branch_comp_1_brlt), .rs2(RegFile_read_data_2));
  Multiplexer #(.width(32), .enable("false")) multiplexer_3 (
    .in0(RegFile_read_data_1), .in1(register_2_q), .out(multiplexer_3_out), .sel(control_logic_1_asel));
  Multiplexer #(.width(32), .enable("false")) multiplexer_4 (
    .in0(RegFile_read_data_2), .in1(IMM), .out(multiplexer_4_out), .sel(control_logic_1_bsel));
  alu Arithmetic_Logic_Unit (
    .Result(ALU_RESULT), .ALUSel(control_logic_1_alusel), .A(multiplexer_3_out), .B(multiplexer_4_out));
  Register #(.width(32)) register_3 (.D(PC_PLUS_4), .clk(CLOCK), .Q(register_3_q));  // open: en, clr
  // mem_main DMEM: pin names not known; wires that end beside it: ALU_RESULT, RegFile_read_data_2, CLOCK, CLOCK, control_logic_1_memrw, DMEM_READ_DATA
  Multiplexer #(.select(2), .width(32), .enable("false")) multiplexer_5 (
    .in0(ALU_RESULT), .in1(DMEM_READ_DATA), .in2(register_3_q), .out(WB_DATA), .sel(control_logic_1_wbsel));  // open: in3

  // Other names for the same wires on the sheet: clk = CLOCK

  // Notes on the sheet:
  //   Output
  //   IMEM (do **NOT** move this)
  //   Inputs
  //   Inputs/Outputs for testing. Do **NOT** move these.
endmodule
