// Logisim project imm_gen.circ as structural Verilog: 1 circuit, main circuit imm_gen
module imm_gen (
  input  [31:0] inst,
  input  [2:0] ImmSel,
  output [31:0] imm
);

  wire [31:11] imm_I, imm_S;
  wire [31:12] imm_SB;
  wire [31:20] imm_UJ;

  assign imm_I = {{20{inst[31]}}, inst[31]};  // Bit_Extender bit_extender_1
  assign imm_S = {{20{inst[31]}}, inst[31]};  // Bit_Extender bit_extender_2
  assign imm_SB = {{19{inst[31]}}, inst[31]};  // Bit_Extender bit_extender_3
  assign imm_UJ = {{11{inst[31]}}, inst[31]};  // Bit_Extender bit_extender_4
  Multiplexer #(.select(3), .width(32), .enable("false")) multiplexer_1 (
    .in0({imm_I, inst[30:20]}), .in1({imm_S, inst[30:25], inst[11:7]}),
    .in2({imm_SB, inst[7], inst[30:25], inst[11:8], 1'b0}), .in3({inst[31:12], {12{1'b0}}}),
    .in4({imm_UJ, inst[19:12], inst[20], inst[30:21], 1'b0}), .out(imm), .sel(ImmSel));  // open: in5, in6, in7

  // Other names for the same wires on the sheet: imm_U[31:12] = inst[31:12]; INST_31 = inst[31];
  //   imm_I[10:0] = inst[30:20]; imm_UJ[19:1] = {inst[19:12], inst[20], inst[30:21]}; INST_24_21[3:0] = inst[24:21];
  //   INST_30_20[10:0] = inst[30:20]; imm_S[10:0] = {inst[30:25], inst[11:7]};
  //   imm_SB[11:1] = {inst[7], inst[30:25], inst[11:8]}; INST_30_25[5:0] = inst[30:25]; INST_20 = inst[20];
  //   INST_19_12[7:0] = inst[19:12]; INST_7 = inst[7]; INST_11_8[3:0] = inst[11:8]

  // Notes on the sheet:
  //   INPUTS to your circuit
  //   DON'T CHANGE THE LOCATIONS OF THE INPUTS AND OUTPUTS!
  //   OUTPUT from your circuit
endmodule
